// Logisim project circuit_F.3.circ as structural Verilog
module main (
  input  in_1,
  input  in_2,
  output out_3,
  output out_4,
  output out_5,
  output out_6
);

  wire not_1_out, not_2_out;

  not not_1 (not_1_out, in_1);
  not not_2 (not_2_out, in_2);
  and and_1 (out_3, not_1_out, not_2_out);
  and and_2 (out_4, in_1, not_2_out);
  and and_3 (out_5, not_1_out, in_2);
  and and_4 (out_6, in_1, in_2);
endmodule

module decoder_1_2 (
  input  in_1,
  output out_2,
  output out_3
);

  not not_1 (out_2, in_1);

  assign out_3 = in_1;
endmodule

module decoder_2_4 (
  input  in_1,
  input  in_2,
  output out_3,
  output out_4,
  output out_5,
  output out_6
);

  wire not_1_out, not_2_out;

  not not_1 (not_1_out, in_1);
  not not_2 (not_2_out, in_2);
  and and_1 (out_3, not_1_out, not_2_out);
  and and_2 (out_4, in_1, not_2_out);
  and and_3 (out_5, not_1_out, in_2);
  and and_4 (out_6, in_1, in_2);
endmodule

module decoder_3_8 (
  input  in_1,
  input  in_2,
  input  in_3,
  output out_4,
  output out_5,
  output out_6,
  output out_7,
  output out_8,
  output out_9,
  output out_10,
  output out_11
);

  wire decoder_2_4_1_out_3, decoder_2_4_1_out_4, decoder_2_4_1_out_5, decoder_2_4_1_out_6,
       decoder_2_4_2_out_3, decoder_2_4_2_out_4, decoder_2_4_2_out_5, decoder_2_4_2_out_6;

  decoder_2_4 decoder_2_4_1 (
    .in_1(in_1), .in_2(in_2), .out_3(decoder_2_4_1_out_3), .out_4(decoder_2_4_1_out_4),
    .out_5(decoder_2_4_1_out_5), .out_6(decoder_2_4_1_out_6));
  decoder_2_4 decoder_2_4_2 (
    .in_1(in_2), .in_2(in_3), .out_3(decoder_2_4_2_out_3), .out_4(decoder_2_4_2_out_4),
    .out_5(decoder_2_4_2_out_5), .out_6(decoder_2_4_2_out_6));
  and and_1 (out_4, decoder_2_4_1_out_3, decoder_2_4_2_out_3);
  and and_2 (out_5, decoder_2_4_1_out_4, decoder_2_4_2_out_3);
  and and_3 (out_6, decoder_2_4_1_out_5, decoder_2_4_2_out_4);
  and and_4 (out_7, decoder_2_4_1_out_6, decoder_2_4_2_out_4);
  and and_5 (out_8, decoder_2_4_1_out_3, decoder_2_4_2_out_5);
  and and_6 (out_9, decoder_2_4_1_out_4, decoder_2_4_2_out_5);
  and and_7 (out_10, decoder_2_4_1_out_5, decoder_2_4_2_out_6);
  and and_8 (out_11, decoder_2_4_1_out_6, decoder_2_4_2_out_6);
endmodule

module xor_fully_customized (
  input  in_1,
  input  in_2,
  input  in_3,
  output out_4
);

  wire transistor_1_out;

  Transistor transistor_1 (.in(in_1), .out(transistor_1_out), .gate(in_2));
  Transistor #(.\type ("n")) transistor_2 (.in(1'b0), .out(transistor_1_out), .gate(in_2));
  Transistor transistor_3 (.in(in_2), .out(out_4), .gate(in_3));
  Transistor #(.\type ("n")) transistor_4 (.in(transistor_1_out), .out(out_4), .gate(in_3));
  Transistor transistor_5 (.in(in_3), .out(out_4), .gate(in_2));
  Transistor #(.\type ("n")) transistor_6 (.in(in_3), .out(out_4), .gate(transistor_1_out));
endmodule

module xnor_fully_customized (
  input  in_1,
  input  in_2,
  input  in_3,
  output out_4
);

  wire transistor_1_out;

  Transistor #(.\type ("n")) transistor_1 (.in(1'b0), .out(transistor_1_out), .gate(in_1));
  Transistor transistor_2 (.in(in_2), .out(transistor_1_out), .gate(in_1));
  Transistor #(.\type ("n")) transistor_3 (.in(in_1), .out(out_4), .gate(in_3));
  Transistor transistor_4 (.in(transistor_1_out), .out(out_4), .gate(in_3));
  Transistor #(.\type ("n")) transistor_5 (.in(in_3), .out(out_4), .gate(in_1));
  Transistor transistor_6 (.in(in_3), .out(out_4), .gate(transistor_1_out));
endmodule

module decoder_7segment (
  input  A0,
  input  A1,
  input  A2,
  input  A3,
  output out_5,
  output out_6,
  output out_7,
  output out_8,
  output out_9,
  output out_10,
  output out_11,
  output out_12,
  output out_13,
  output out_14,
  output out_15,
  output out_16,
  output out_17,
  output out_18,
  output out_19,
  output out_20
);

  wire a_out, b_out, c_out, d_out, decoder_1_2_1_out_2, decoder_1_2_1_out_3, decoder_3_8_1_out_4,
       decoder_3_8_1_out_5, decoder_3_8_1_out_6, decoder_3_8_1_out_7, decoder_3_8_1_out_8,
       decoder_3_8_1_out_9, decoder_3_8_1_out_10, decoder_3_8_1_out_11, e_out, f_out, g_out, h_out;

  decoder_3_8 decoder_3_8_1 (
    .in_1(A0), .in_2(A1), .in_3(A2), .out_4(decoder_3_8_1_out_4), .out_5(decoder_3_8_1_out_5),
    .out_6(decoder_3_8_1_out_6), .out_7(decoder_3_8_1_out_7), .out_8(decoder_3_8_1_out_8),
    .out_9(decoder_3_8_1_out_9), .out_10(decoder_3_8_1_out_10), .out_11(decoder_3_8_1_out_11));
  decoder_1_2 decoder_1_2_1 (.in_1(A3), .out_2(decoder_1_2_1_out_2), .out_3(decoder_1_2_1_out_3));
  and C0 (out_5, decoder_3_8_1_out_4, decoder_1_2_1_out_2);
  and C1 (out_6, decoder_3_8_1_out_5, decoder_1_2_1_out_2);
  and C2 (out_7, decoder_3_8_1_out_6, decoder_1_2_1_out_2);
  and C3 (out_8, decoder_3_8_1_out_7, decoder_1_2_1_out_2);
  and C4 (out_9, decoder_3_8_1_out_8, decoder_1_2_1_out_2);
  and C5 (out_10, decoder_3_8_1_out_9, decoder_1_2_1_out_2);
  and C6 (out_11, decoder_3_8_1_out_10, decoder_1_2_1_out_2);
  and C7 (out_12, decoder_3_8_1_out_11, decoder_1_2_1_out_2);
  and C8 (out_13, decoder_3_8_1_out_4, decoder_1_2_1_out_3);
  and C9 (out_14, decoder_3_8_1_out_5, decoder_1_2_1_out_3);
  and C10 (out_15, decoder_3_8_1_out_6, decoder_1_2_1_out_3);
  and C11 (out_16, decoder_3_8_1_out_7, decoder_1_2_1_out_3);
  and C12 (out_17, decoder_3_8_1_out_8, decoder_1_2_1_out_3);
  and C13 (out_18, decoder_3_8_1_out_9, decoder_1_2_1_out_3);
  and C14 (out_19, decoder_3_8_1_out_10, decoder_1_2_1_out_3);
  and C16 (out_20, decoder_3_8_1_out_11, decoder_1_2_1_out_3);
  or h (h_out, out_15, out_16, out_17, out_18, out_19, out_20);
  or g (g_out, out_7, out_8, out_9, out_10, out_11, out_13, out_14);
  or f (f_out, out_5, out_9, out_10, out_11, out_13, out_14);
  or e (e_out, out_5, out_7, out_11, out_13);
  or d (d_out, out_5, out_7, out_8, out_10, out_11, out_13, out_14);
  or c (c_out, out_5, out_6, out_8, out_9, out_10, out_11, out_12, out_13, out_14);
  or b (b_out, out_5, out_6, out_7, out_8, out_9, out_12, out_13, out_14);
  or a (a_out, out_5, out_7, out_8, out_10, out_11, out_12, out_13, out_14);
  _7_Segment_Display u_7_segment_display_1 (
    .g(g_out), .f(f_out), .a(a_out), .b(b_out), .e(e_out), .d(d_out), .c(c_out), .dp(h_out));
endmodule

module decoder_hex_digit (
  input  A0,
  input  A1,
  input  A2,
  input  A3,
  output out_5,
  output out_6,
  output out_7,
  output out_8,
  output out_9,
  output out_10,
  output out_11
);

  wire C0_out, C1_out, C2_out, C3_out, C4_out, C5_out, C6_out, C7_out, C8_out, C9_out, C10_out, C11_out,
       C12_out, C13_out, C14_out, C15_out, decoder_1_2_1_out_2, decoder_1_2_1_out_3, decoder_3_8_1_out_4,
       decoder_3_8_1_out_5, decoder_3_8_1_out_6, decoder_3_8_1_out_7, decoder_3_8_1_out_8,
       decoder_3_8_1_out_9, decoder_3_8_1_out_10, decoder_3_8_1_out_11;

  decoder_3_8 decoder_3_8_1 (
    .in_1(A0), .in_2(A1), .in_3(A2), .out_4(decoder_3_8_1_out_4), .out_5(decoder_3_8_1_out_5),
    .out_6(decoder_3_8_1_out_6), .out_7(decoder_3_8_1_out_7), .out_8(decoder_3_8_1_out_8),
    .out_9(decoder_3_8_1_out_9), .out_10(decoder_3_8_1_out_10), .out_11(decoder_3_8_1_out_11));
  decoder_1_2 decoder_1_2_1 (.in_1(A3), .out_2(decoder_1_2_1_out_2), .out_3(decoder_1_2_1_out_3));
  and C0 (C0_out, decoder_3_8_1_out_4, decoder_1_2_1_out_2);
  and C1 (C1_out, decoder_3_8_1_out_5, decoder_1_2_1_out_2);
  and C2 (C2_out, decoder_3_8_1_out_6, decoder_1_2_1_out_2);
  and C3 (C3_out, decoder_3_8_1_out_7, decoder_1_2_1_out_2);
  and C4 (C4_out, decoder_3_8_1_out_8, decoder_1_2_1_out_2);
  and C5 (C5_out, decoder_3_8_1_out_9, decoder_1_2_1_out_2);
  and C6 (C6_out, decoder_3_8_1_out_10, decoder_1_2_1_out_2);
  and C7 (C7_out, decoder_3_8_1_out_11, decoder_1_2_1_out_2);
  and C8 (C8_out, decoder_3_8_1_out_4, decoder_1_2_1_out_3);
  and C9 (C9_out, decoder_3_8_1_out_5, decoder_1_2_1_out_3);
  and C10 (C10_out, decoder_3_8_1_out_6, decoder_1_2_1_out_3);
  and C11 (C11_out, decoder_3_8_1_out_7, decoder_1_2_1_out_3);
  and C12 (C12_out, decoder_3_8_1_out_8, decoder_1_2_1_out_3);
  and C13 (C13_out, decoder_3_8_1_out_9, decoder_1_2_1_out_3);
  and C14 (C14_out, decoder_3_8_1_out_10, decoder_1_2_1_out_3);
  and C15 (C15_out, decoder_3_8_1_out_11, decoder_1_2_1_out_3);
  or g (out_11, C2_out, C3_out, C4_out, C5_out, C6_out, C8_out, C9_out, C10_out, C11_out, C13_out, C14_out, C15_out);
  or f (out_10, C0_out, C4_out, C5_out, C6_out, C8_out, C9_out, C10_out, C11_out, C12_out, C14_out, C15_out);
  or e (out_9, C0_out, C2_out, C6_out, C8_out, C10_out, C11_out, C12_out, C13_out, C14_out, C15_out);
  or d (out_8, C0_out, C2_out, C3_out, C5_out, C6_out, C8_out, C9_out, C11_out, C12_out, C13_out, C14_out);
  or c (out_7, C0_out, C1_out, C3_out, C4_out, C5_out, C6_out, C7_out, C8_out, C9_out, C10_out, C11_out, C13_out);
  or b (out_6, C0_out, C1_out, C2_out, C3_out, C4_out, C7_out, C8_out, C9_out, C10_out, C13_out);
  or a (out_5, C0_out, C2_out, C3_out, C5_out, C6_out, C7_out, C8_out, C9_out, C10_out, C12_out, C14_out, C15_out);
  _7_Segment_Display u_7_segment_display_1 (
    .g(out_11), .f(out_10), .a(out_5), .b(out_6), .e(out_9), .d(out_8), .c(out_7));  // open: dp
endmodule

module encoder_16to4 (
  input  A0,
  input  in_2,
  input  in_3,
  input  in_4,
  input  A4,
  input  in_6,
  input  in_7,
  input  in_8,
  input  A8,
  input  in_10,
  input  in_11,
  input  in_12,
  input  A12,
  input  in_14,
  input  in_15,
  input  in_16,
  output out_17,
  output out_18,
  output out_19,
  output out_20
);

  or B0 (out_17, in_2, in_4, in_6, in_8, in_10, in_12, in_14, in_16);
  or B1 (out_18, in_3, in_4, in_7, in_8, in_11, in_12, in_15, in_16);
  or B2 (out_19, A4, in_6, in_7, in_8, A12, in_14, in_15, in_16);
  or B3 (out_20, A8, in_10, in_11, in_12, A12, in_14, in_15, in_16);
endmodule

module encoder_4to2 (
  input  A0,
  input  A1,
  input  A2,
  input  A3,
  output Y0,
  output Y1
);

  or or_1 (Y0, A1, A3);
  or or_2 (Y1, A2, A3);
endmodule

module prior_encoder_4to2 (
  input  A0,
  input  A1,
  input  A2,
  input  A3,
  output Y0,
  output Y1
);

  wire and_1_out, and_2_out;

  and and_1 (and_1_out, A1, ~A2, ~A3);  // AND_Gate
  and and_2 (and_2_out, A2, ~A3);  // AND_Gate
  or or_1 (Y0, and_1_out, A3);
  or or_2 (Y1, and_2_out, A3);
endmodule

module prior_encoder_16to4 (
);

  wire prior_encoder_4to2_1_y0, prior_encoder_4to2_1_y1, prior_encoder_4to2_2_y0, prior_encoder_4to2_2_y1,
       prior_encoder_4to2_3_y0, prior_encoder_4to2_3_y1, prior_encoder_4to2_4_y0, prior_encoder_4to2_4_y1;

  prior_encoder_4to2 prior_encoder_4to2_1 (
    .Y0(prior_encoder_4to2_1_y0), .Y1(prior_encoder_4to2_1_y1));  // open: A0, A1, A2, A3
  prior_encoder_4to2 prior_encoder_4to2_2 (
    .Y0(prior_encoder_4to2_2_y0), .Y1(prior_encoder_4to2_2_y1));  // open: A0, A1, A2, A3
  prior_encoder_4to2 prior_encoder_4to2_3 (
    .Y0(prior_encoder_4to2_3_y0), .Y1(prior_encoder_4to2_3_y1));  // open: A0, A1, A2, A3
  prior_encoder_4to2 prior_encoder_4to2_4 (
    .Y0(prior_encoder_4to2_4_y0), .Y1(prior_encoder_4to2_4_y1));  // open: A0, A1, A2, A3
  // OR_Gate or_1 has open pins: in0=prior_encoder_4to2_1_y0, in1=prior_encoder_4to2_1_y1, out=open
  // OR_Gate or_2 has open pins: in0=prior_encoder_4to2_2_y0, in1=prior_encoder_4to2_2_y1, out=open
  // OR_Gate or_3 has open pins: in0=prior_encoder_4to2_3_y0, in1=prior_encoder_4to2_3_y1, out=open
  // OR_Gate or_4 has open pins: in0=prior_encoder_4to2_4_y0, in1=prior_encoder_4to2_4_y1, out=open
endmodule

module mux_2to1 (
  input  D0,
  input  S,
  input  D1,
  output out_4
);

  wire and_1_out, and_2_out, decoder_1_2_1_out_2, decoder_1_2_1_out_3;

  decoder_1_2 decoder_1_2_1 (.in_1(S), .out_2(decoder_1_2_1_out_2), .out_3(decoder_1_2_1_out_3));
  and and_1 (and_1_out, D0, decoder_1_2_1_out_2);
  and and_2 (and_2_out, decoder_1_2_1_out_3, D1);
  or or_1 (out_4, and_1_out, and_2_out);
endmodule

module mux_4to1 (
  input  in_1,
  input  in_2,
  input  in_3,
  input  in_4,
  input  in_5,
  input  in_6,
  input  in_7,
  output out_8
);

  wire and_1_out, and_2_out, and_3_out, and_4_out, decoder_3_8_1_out_4, decoder_3_8_1_out_5,
       decoder_3_8_1_out_6, decoder_3_8_1_out_7;

  decoder_3_8 decoder_3_8_1 (
    .in_1(in_3), .in_2(in_4), .in_3(in_5), .out_4(decoder_3_8_1_out_4), .out_5(decoder_3_8_1_out_5),
    .out_6(decoder_3_8_1_out_6), .out_7(decoder_3_8_1_out_7));  // open: out_8, out_9, out_10, out_11
  and and_1 (and_1_out, in_1, decoder_3_8_1_out_4);
  and and_2 (and_2_out, in_2, decoder_3_8_1_out_5);
  and and_3 (and_3_out, decoder_3_8_1_out_6, in_6);
  and and_4 (and_4_out, decoder_3_8_1_out_7, in_7);
  or or_1 (out_8, and_1_out, and_2_out, and_3_out, and_4_out);
endmodule

module comparator_4bit (
  input  in_1,
  input  in_2,
  input  in_3,
  input  in_4,
  input  in_5,
  input  in_6,
  input  in_7,
  input  in_8
);

  wire and_1_out, xnor_1_out, xnor_2_out, xnor_3_out, xnor_4_out;

  xnor xnor_1 (xnor_1_out, in_1, in_2);
  xnor xnor_2 (xnor_2_out, in_3, in_4);
  xnor xnor_3 (xnor_3_out, in_5, in_6);
  xnor xnor_4 (xnor_4_out, in_7, in_8);
  and and_1 (and_1_out, xnor_1_out, xnor_2_out, xnor_3_out, xnor_4_out);
  LED led_1 (.in(and_1_out));
endmodule

module adder_1_bit_full (
  input  Cin,
  input  A,
  input  B,
  output S,
  output Cout
);

  wire and_1_out, and_2_out, or_1_out, xor_1_out;

  and and_1 (and_1_out, ~Cin, A, B);  // AND_Gate
  or or_1 (or_1_out, A, B);
  xor xor_1 (xor_1_out, A, B);
  xor xor_2 (S, Cin, xor_1_out);
  or or_2 (Cout, and_1_out, and_2_out);
  and and_2 (and_2_out, Cin, or_1_out);
endmodule

module adder_1bit_half (
  input  A,
  input  B,
  output S,
  output C
);

  xor xor_1 (S, A, B);
  and and_1 (C, A, B);
endmodule

module adder_1bit_full_2 (
  input  Cin,
  input  A,
  input  B,
  output S,
  output Cout
);

  wire adder_1bit_half_1_c, adder_1bit_half_1_s, adder_1bit_half_2_c;

  adder_1bit_half adder_1bit_half_1 (.A(A), .B(B), .S(adder_1bit_half_1_s), .C(adder_1bit_half_1_c));
  adder_1bit_half adder_1bit_half_2 (.A(Cin), .B(adder_1bit_half_1_s), .S(S), .C(adder_1bit_half_2_c));
  xor xor_1 (Cout, adder_1bit_half_2_c, adder_1bit_half_1_c);
endmodule

module adder_4bit_full (
  input  A3,
  input  B3,
  input  A2,
  input  B2,
  input  A1,
  input  B1,
  input  A0,
  input  B0,
  input  C0,
  output C4,
  output S3,
  output S2,
  output S1,
  output S0
);

  wire adder_1bit_full_2_2_cout, adder_1bit_full_2_3_cout, adder_1bit_full_2_4_cout;

  adder_1bit_full_2 adder_1bit_full_2_1 (.Cin(adder_1bit_full_2_2_cout), .A(A3), .B(B3), .S(S3), .Cout(C4));
  LED led_1 (.in(adder_1bit_full_2_2_cout));
  adder_1bit_full_2 adder_1bit_full_2_2 (
    .Cin(adder_1bit_full_2_3_cout), .A(A2), .B(B2), .S(S2), .Cout(adder_1bit_full_2_2_cout));
  LED led_2 (.in(adder_1bit_full_2_3_cout));
  adder_1bit_full_2 adder_1bit_full_2_3 (
    .Cin(adder_1bit_full_2_4_cout), .A(A1), .B(B1), .S(S1), .Cout(adder_1bit_full_2_3_cout));
  LED led_3 (.in(adder_1bit_full_2_4_cout));
  adder_1bit_full_2 adder_1bit_full_2_4 (.Cin(C0), .A(A0), .B(B0), .S(S0), .Cout(adder_1bit_full_2_4_cout));
endmodule

module subtractor_4bit_full (
  input  A3,
  input  B3,
  input  A2,
  input  B2,
  input  A1,
  input  B1,
  input  A0,
  input  B0,
  input  C0,
  output C4,
  output S3,
  output S2,
  output S1,
  output S0
);

  wire A_out_5, A_out_6, A_out_7, A_out_8, A_out_9, A_out_10, A_out_11, B_out_5, B_out_6, B_out_7, B_out_8,
       B_out_9, B_out_10, B_out_11, decoder_hex_digit_1_out_5, decoder_hex_digit_1_out_6,
       decoder_hex_digit_1_out_7, decoder_hex_digit_1_out_8, decoder_hex_digit_1_out_9,
       decoder_hex_digit_1_out_10, decoder_hex_digit_1_out_11, substractor_1bit_full_2_c_borrow_out,
       substractor_1bit_full_3_c_borrow_out, substractor_1bit_full_4_c_borrow_out;

  LED led_1 (.in(C4));
  substractor_1bit_full substractor_1bit_full_1 (
    .C_borrow_in(substractor_1bit_full_2_c_borrow_out), .A(A3), .B(B3), .S(S3), .C_borrow_out(C4));
  LED led_2 (.in(substractor_1bit_full_2_c_borrow_out));
  substractor_1bit_full substractor_1bit_full_2 (
    .C_borrow_in(substractor_1bit_full_3_c_borrow_out), .A(A2), .B(B2), .S(S2),
    .C_borrow_out(substractor_1bit_full_2_c_borrow_out));
  LED led_3 (.in(substractor_1bit_full_3_c_borrow_out));
  substractor_1bit_full substractor_1bit_full_3 (
    .C_borrow_in(substractor_1bit_full_4_c_borrow_out), .A(A1), .B(B1), .S(S1),
    .C_borrow_out(substractor_1bit_full_3_c_borrow_out));
  LED led_4 (.in(substractor_1bit_full_4_c_borrow_out));
  substractor_1bit_full substractor_1bit_full_4 (
    .C_borrow_in(C0), .A(A0), .B(B0), .S(S0), .C_borrow_out(substractor_1bit_full_4_c_borrow_out));
  decoder_hex_digit A (
    .A0(A0), .A1(A1), .A2(A2), .A3(A3), .out_5(A_out_5), .out_6(A_out_6), .out_7(A_out_7), .out_8(A_out_8),
    .out_9(A_out_9), .out_10(A_out_10), .out_11(A_out_11));
  decoder_hex_digit B (
    .A0(B0), .A1(B1), .A2(B2), .A3(B3), .out_5(B_out_5), .out_6(B_out_6), .out_7(B_out_7), .out_8(B_out_8),
    .out_9(B_out_9), .out_10(B_out_10), .out_11(B_out_11));
  decoder_hex_digit decoder_hex_digit_1 (
    .A0(S0), .A1(S1), .A2(S2), .A3(S3), .out_5(decoder_hex_digit_1_out_5), .out_6(decoder_hex_digit_1_out_6),
    .out_7(decoder_hex_digit_1_out_7), .out_8(decoder_hex_digit_1_out_8), .out_9(decoder_hex_digit_1_out_9),
    .out_10(decoder_hex_digit_1_out_10), .out_11(decoder_hex_digit_1_out_11));
  _7_Segment_Display u_7_segment_display_1 (
    .g(A_out_11), .f(A_out_10), .a(A_out_5), .b(A_out_6), .e(A_out_9), .d(A_out_8), .c(A_out_7));  // open: dp
  _7_Segment_Display u_7_segment_display_2 (
    .g(B_out_11), .f(B_out_10), .a(B_out_5), .b(B_out_6), .e(B_out_9), .d(B_out_8), .c(B_out_7));  // open: dp
  _7_Segment_Display u_7_segment_display_3 (
    .g(decoder_hex_digit_1_out_11), .f(decoder_hex_digit_1_out_10), .a(decoder_hex_digit_1_out_5),
    .b(decoder_hex_digit_1_out_6), .e(decoder_hex_digit_1_out_9), .d(decoder_hex_digit_1_out_8),
    .c(decoder_hex_digit_1_out_7));  // open: dp
endmodule

module subtractor_1bit_half (
  input  A,
  input  B,
  output S,
  output C
);

  xor xor_1 (S, A, B);
  and and_1 (C, ~A, B);  // AND_Gate
endmodule

module substractor_1bit_full (
  input  C_borrow_in,
  input  A,
  input  B,
  output S,
  output C_borrow_out
);

  wire subtractor_1bit_half_1_c, subtractor_1bit_half_1_s, subtractor_1bit_half_2_c;

  subtractor_1bit_half subtractor_1bit_half_1 (
    .A(A), .B(B), .S(subtractor_1bit_half_1_s), .C(subtractor_1bit_half_1_c));
  subtractor_1bit_half subtractor_1bit_half_2 (
    .A(subtractor_1bit_half_1_s), .B(C_borrow_in), .S(S), .C(subtractor_1bit_half_2_c));
  xor xor_1 (C_borrow_out, subtractor_1bit_half_2_c, subtractor_1bit_half_1_c);
endmodule

module adder_4bit_original_code (
  input  A4,
  input  A3,
  input  A2,
  input  A1,
  input  A0,
  input  B4,
  input  B3,
  input  B2,
  input  B1,
  input  B0,
  output out_11,
  output out_12,
  output out_13,
  output out_14,
  output out_15
);

  wire A_out_5, A_out_6, A_out_7, A_out_8, A_out_9, A_out_10, A_out_11, adder_4bit_full_1_s0,
       adder_4bit_full_1_s1, adder_4bit_full_1_s2, adder_4bit_full_1_s3, and_1_out, and_2_out, and_3_out,
       and_4_out, and_5_out, and_6_out, and_7_out, and_8_out, and_9_out, and_10_out, and_11_out, and_12_out,
       and_13_out, and_14_out, and_15_out, and_16_out, and_17_out, subtractor_4bit_full_1_c4,
       subtractor_4bit_full_1_s0, subtractor_4bit_full_1_s1, subtractor_4bit_full_1_s2,
       subtractor_4bit_full_1_s3, xor_1_out;

  xor xor_1 (xor_1_out, A4, B4);
  and and_1 (and_1_out, ~xor_1_out, A3);  // AND_Gate
  and and_2 (and_2_out, ~xor_1_out, A2);  // AND_Gate
  and and_3 (and_3_out, ~xor_1_out, A1);  // AND_Gate
  and and_4 (and_4_out, ~xor_1_out, A0);  // AND_Gate
  and and_5 (and_5_out, ~xor_1_out, B3);  // AND_Gate
  and and_6 (and_6_out, ~xor_1_out, B2);  // AND_Gate
  and and_7 (and_7_out, ~xor_1_out, B1);  // AND_Gate
  and and_8 (and_8_out, ~xor_1_out, B0);  // AND_Gate
  and and_9 (and_9_out, xor_1_out, A3);
  and and_10 (and_10_out, xor_1_out, A2);
  and and_11 (and_11_out, xor_1_out, A1);
  and and_12 (and_12_out, xor_1_out, A0);
  and and_13 (and_13_out, xor_1_out, B3);
  and and_14 (and_14_out, xor_1_out, B2);
  and and_15 (and_15_out, xor_1_out, B1);
  and and_16 (and_16_out, xor_1_out, B0);
  adder_4bit_full adder_4bit_full_1 (
    .A3(and_1_out), .B3(and_5_out), .A2(and_2_out), .B2(and_6_out), .A1(and_3_out), .B1(and_7_out),
    .A0(and_4_out), .B0(and_8_out), .S3(adder_4bit_full_1_s3), .S2(adder_4bit_full_1_s2),
    .S1(adder_4bit_full_1_s1), .S0(adder_4bit_full_1_s0));  // open: C0, C4
  subtractor_4bit_full subtractor_4bit_full_1 (
    .A3(and_9_out), .B3(and_13_out), .A2(and_10_out), .B2(and_14_out), .A1(and_11_out), .B1(and_15_out),
    .A0(and_12_out), .B0(and_16_out), .C4(subtractor_4bit_full_1_c4), .S3(subtractor_4bit_full_1_s3),
    .S2(subtractor_4bit_full_1_s2), .S1(subtractor_4bit_full_1_s1), .S0(subtractor_4bit_full_1_s0));  // open: C0
  and and_17 (and_17_out, ~subtractor_4bit_full_1_c4, subtractor_4bit_full_1_s3);  // AND_Gate
  or or_1 (out_12, adder_4bit_full_1_s3, and_17_out);
  or or_2 (out_13, adder_4bit_full_1_s2, subtractor_4bit_full_1_s2);
  or or_3 (out_14, adder_4bit_full_1_s1, subtractor_4bit_full_1_s1);
  or or_4 (out_15, adder_4bit_full_1_s0, subtractor_4bit_full_1_s0);
  decoder_hex_digit A (
    .A0(out_15), .A1(out_14), .A2(out_13), .A3(out_12), .out_5(A_out_5), .out_6(A_out_6), .out_7(A_out_7),
    .out_8(A_out_8), .out_9(A_out_9), .out_10(A_out_10), .out_11(A_out_11));
  _7_Segment_Display u_7_segment_display_1 (
    .g(A_out_11), .f(A_out_10), .a(A_out_5), .b(A_out_6), .e(A_out_9), .d(A_out_8), .c(A_out_7));  // open: dp
endmodule

module s_r_latch (
  input  in_1,
  input  in_2,
  output out_3,
  output out_4
);

  nor nor_1 (out_3, in_1, out_4);
  nor nor_2 (out_4, out_3, in_2);
endmodule

module d_latch (
  input  D,
  input  WE,
  output Q,
  output Qbar
);

  wire and_1_out, and_2_out;

  and and_1 (and_1_out, D, WE);
  and and_2 (and_2_out, WE, ~D);  // AND_Gate
  s_r_latch s_r_latch_1 (.in_1(and_1_out), .in_2(and_2_out), .out_3(Q), .out_4(Qbar));
endmodule

module d_slatch_reset (
  input  RESET,
  input  WE,
  input  D,
  output out_4,
  output out_5
);

  wire and_1_out, and_2_out, not_1_out, not_2_out, or_1_out, or_2_out;

  or or_1 (or_1_out, RESET, WE);
  or or_2 (or_2_out, RESET, D);
  and and_1 (and_1_out, or_2_out, or_1_out);
  and and_2 (and_2_out, or_1_out, ~or_2_out);  // AND_Gate
  // AND_Gate and_3 has open pins: in0=RESET, in1=not_1_out, out=open
  // AND_Gate and_4 has open pins: in0=not_2_out, in1=RESET, out=open
  not not_1 (not_1_out, out_4);
  not not_2 (not_2_out, out_5);
  s_r_latch s_r_latch_1 (.in_1(and_1_out), .in_2(and_2_out), .out_3(out_4), .out_4(out_5));
endmodule

module d_flip_flop (
  input  in_1,
  output Q
);

  wire clock_1_out, d_latch_1_q, not_1_out;

  Clock clock_1 (.out(clock_1_out));
  not not_1 (not_1_out, clock_1_out);
  d_latch d_latch_1 (.D(in_1), .WE(not_1_out), .Q(d_latch_1_q));  // open: Qbar
  d_latch d_latch_2 (.D(d_latch_1_q), .WE(not_1_out), .Q(Q));  // open: Qbar
endmodule
