// Logisim project circuit_F.5.circ as structural Verilog
module rom_3x2 (
  input  in_1,
  input  in_2,
  input  in_3,
  input  in_4,
  input  in_5,
  input  in_6
);

  wire and_1_out, and_2_out, and_3_out, and_4_out, and_5_out, and_6_out, decoder_1_out0, decoder_1_out1;

  Decoder decoder_1 (.out0(decoder_1_out0), .out1(decoder_1_out1));  // open: sel, en
  and and_1 (and_1_out, in_1, decoder_1_out0);
  and and_2 (and_2_out, decoder_1_out1, in_4);
  // OR_Gate or_1 has open pins: in0=and_2_out, in1=and_1_out, out=open
  and and_3 (and_3_out, in_2, decoder_1_out0);
  and and_4 (and_4_out, decoder_1_out1, in_5);
  // OR_Gate or_2 has open pins: in0=and_4_out, in1=and_3_out, out=open
  and and_5 (and_5_out, in_3, decoder_1_out0);
  and and_6 (and_6_out, decoder_1_out1, in_6);
  // OR_Gate or_3 has open pins: in0=and_6_out, in1=and_5_out, out=open
endmodule
