// Logisim project xnor_Fully_customized.circ as structural Verilog: 1 circuit, main circuit main
module main (
  input  in_1,
  input  in_2,
  input  in_3,
  output out_4
);

  wire transistor_1_out;

  Transistor #(.\type ("n")) transistor_1 (.in(1'b0), .out(transistor_1_out), .gate(in_1));
  Transistor transistor_2 (.in(in_2), .out(transistor_1_out), .gate(in_1));
  Transistor #(.\type ("n")) transistor_3 (.in(in_1), .out(out_4), .gate(in_3));
  Transistor transistor_4 (.in(transistor_1_out), .out(out_4), .gate(in_3));
  Transistor #(.\type ("n")) transistor_5 (.in(in_3), .out(out_4), .gate(in_1));
  Transistor transistor_6 (.in(in_3), .out(out_4), .gate(transistor_1_out));
endmodule
