// Logisim project xnor_half_customized.circ as structural Verilog: 1 circuit, main circuit main
module main (
  input  in_1,
  input  in_2,
  output out_3
);

  wire nand_1_out, or_1_out;

  nand nand_1 (nand_1_out, in_1, in_2);
  or or_1 (or_1_out, in_1, in_2);
  nand nand_2 (out_3, nand_1_out, or_1_out);
endmodule
