// Logisim project xor_Fully_customized.circ as structural Verilog: 1 circuit, main circuit main
module main (
  input  in_1,
  input  in_2,
  input  in_3,
  output out_4
);

  wire transistor_1_out;

  Transistor transistor_1 (.in(in_1), .out(transistor_1_out), .gate(in_2));
  Transistor #(.\type ("n")) transistor_2 (.in(1'b0), .out(transistor_1_out), .gate(in_2));
  Transistor transistor_3 (.in(in_2), .out(out_4), .gate(in_3));
  Transistor #(.\type ("n")) transistor_4 (.in(transistor_1_out), .out(out_4), .gate(in_3));
  Transistor transistor_5 (.in(in_3), .out(out_4), .gate(in_2));
  Transistor #(.\type ("n")) transistor_6 (.in(in_3), .out(out_4), .gate(transistor_1_out));
endmodule
